# Fritzing sketch tuner_arduino (saved by Fritzing 0.9.3b)

parts:
  R1 = Resistor [tolerance=±5% resistance=1k package=THT]
  C1 = Ceramic Capacitor [capacitance=22µF voltage=16V package="100 mil [THT, multilayer]"]
  uC = Arduino Uno (Rev3)
  J1 = female pin header, 8 pins [form="♀ (female)"]

nets:
  N1: R1.Pin_0, uC.D11_PWM/MOSI
  N2: R1.Pin_1, C1.1, J1.pin1
  GND: C1.0, uC.GND, J1.pin5
  N3: uC.A4/SDA, J1.pin3
  N4: uC.A5/SCL, J1.pin2
  N5: uC.D10_PWM/SS, J1.pin7
  N6: uC.5V, J1.pin4
  N7: uC.VIN, J1.pin6

notes:
  AGC
  SCL
  SDA
  +B
  GND
  BT
  LNA
  IF Out
  Control de Tuner Haier con Arduino, Interfaz para controlar vía Arduino la frecuencia y ganancia del Bloque Sintonizador de TV Haier 21", 1.0
